# Fritzing sketch Untitled Sketch (saved by Fritzing 0.9.4)

parts:
  Raspberry_Pi_1 = Raspberry Pi 3 [part_number=RPI-3-V1.2]
  U1 = 640x480 CMOS Color Camera [package=camera_cmos_con]  # not connected
  J2 = Basic Servo
  M1 = DC Motor
  U2 = L298_BRIDGE_DRIVER [package=powerso20]
  J1 = Basic Servo
  Power_plug1 = Power plug  # not connected

nets:
  N1: Raspberry_Pi_1.GPIO20, J2.pulse
  N2: Raspberry_Pi_1.GPIO16, U2.SENSE_B
  N3: Raspberry_Pi_1.GND, U2.NC, U2.OUT4
  N4: Raspberry_Pi_1.GPIO12, J1.pulse
  N5: M1.pin_1, U2.OUT3
  N6: M1.pin_2, U2.IN4
